# Fritzing sketch TeensyBoard (saved by Fritzing 0.6.3b)
breadboards: 1

parts:
  Teensy1 = Teensy 2.0
  J1 = female pin header, 2 pins [form="♀ (female)"]
  J2 = female pin header, 2 pins [form="♀ (female)"]

nets:
  N1: Teensy1.GND, J1.pin2, J2.pin1
  N2: Teensy1.B5, J2.pin2
  N3: Teensy1.B6, J1.pin1
